# Fritzing sketch Arp2 Diagram (saved by Fritzing 1.0.0rc)
breadboards: 1

parts:
  Part2 = Arduino Pro Micro (Clone)
  MIDI_OUT = Audio Jack (TRS) 3.5mm [package="4Ucon 08780 [THT]"]
  MIDI_IN = Audio Jack (TRS) 3.5mm [package="4Ucon 08780 [THT]"]
  LED1 = smd LED [color="Red (633nm)" package="0603 [SMD]"]
  R1 = Resistor [tolerance=±5% resistance=1k package="1206 [SMD]"]
  R2 = Resistor [tolerance=±5% resistance=220 package="1206 [SMD]"]
  D2 = Rectifier Diode [part_number=1N914 package="300 mil [THT]"]
  R3 = Resistor [tolerance=±5% resistance=220 package="0402 [SMD]"]
  6n137_Optocoupler = 6n137 Optocoupler [part_number=6n137 package="DIP (Dual Inline) [THT]"]
  RESET = Pushbutton [package="[THT]"]
  TEMPO = TRIMPOT [maximum_resistance=10kΩ knob_status=50% power=0.5W package=trimpot_pth_s3_lock]
  OCTAVE = TRIMPOT [maximum_resistance=10kΩ knob_status=50% power=0.5W package=trimpot_pth_s3_lock]
  PROBABILITY = TRIMPOT [maximum_resistance=10kΩ knob_status=50% power=0.5W package=trimpot_pth_s3_lock]
  R4 = Resistor [tolerance=±5% power=0.25W resistance=10k package=THT]

nets:
  N1: Part2.TXO, MIDI_OUT.Tip
  N2: Part2.RXI, 6n137_Optocoupler.Vo, R4.Pin_0
  N3: Part2.GND, MIDI_OUT.Sleeve, LED1.cathode
  N4: Part2.D8, R1.Pin_1
  N5: Part2.A0, TEMPO.WIPER
  N6: Part2.A1, PROBABILITY.WIPER
  N7: Part2.A2, OCTAVE.WIPER
  VCC: Part2.VCC, 6n137_Optocoupler.Vcc, TEMPO.CCW, OCTAVE.CW, PROBABILITY.CW, R4.Pin_1
  N8: Part2.RST, RESET.Pin_3, RESET.Pin_4
  N9: MIDI_OUT.Ring, R2.Pin_1
  N10: MIDI_IN.Ring, R3.Pin_1
  N11: MIDI_IN.Tip, D2.anode, 6n137_Optocoupler.Vf-
  N12: LED1.anode, R1.Pin_0
  N13: D2.cathode, R3.Pin_0, 6n137_Optocoupler.Vf+
  N14: 6n137_Optocoupler.GND, RESET.Pin_1, RESET.Pin_2, TEMPO.CW, OCTAVE.CCW, PROBABILITY.CCW

custom parts:
  6n137 Optocoupler: 6n137 fast Optocoupler. With 8 pins on a 300mil dual inline package (DIP) footprint. Ve is strobe input. Output is inverting.
